// Logisim project control-logic.circ as structural Verilog: 1 circuit, main circuit control_logic
module control_logic (
  input  [31:0] inst,
  input  BrEq,
  input  BrLt,
  output PCSel,
  output RegWEn,
  output [2:0] ImmSel,
  output BrUn,
  output ASel,
  output BSel,
  output [3:0] ALUSel,
  output MemRW,
  output [1:0] WBSel,
  output CSRSel,
  output CSRWen
);

  wire comparator_1_eq, comparator_2_eq, comparator_3_eq, comparator_4_eq, comparator_5_eq, comparator_6_eq,
       comparator_7_eq, comparator_8_eq, comparator_9_eq, comparator_11_eq, comparator_12_eq,
       comparator_13_eq, comparator_14_eq, comparator_15_eq, comparator_18_eq, comparator_19_eq,
       comparator_20_eq, comparator_21_eq, comparator_22_eq, comparator_23_eq, comparator_24_eq,
       comparator_25_eq, comparator_26_eq, comparator_27_eq, comparator_28_eq, comparator_29_eq,
       comparator_30_eq, comparator_31_eq, comparator_32_eq, comparator_33_eq, multiplexer_2_out,
       multiplexer_6_out, not_1_out, not_2_out, or_1_out, or_2_out, or_3_out, or_4_out, or_6_out, or_7_out,
       or_8_out, or_9_out;
  wire [1:0] multiplexer_16_out;
  wire [3:0] multiplexer_1_out, multiplexer_3_out, multiplexer_4_out, multiplexer_5_out, multiplexer_10_out,
       multiplexer_15_out;
  wire [15:0] rom_1_data;

  not not_1 (not_1_out, BrLt);
  Comparator #(.mode("unsigned"), .width(7)) comparator_1 (
    .a(inst[31:25]), .b(7'b0000001), .eq(comparator_1_eq));  // open: gt, lt
  Comparator #(.mode("unsigned"), .width(7)) comparator_2 (
    .a(inst[6:0]), .b(7'b0010011), .eq(comparator_2_eq));  // open: gt, lt
  Comparator #(.mode("unsigned"), .width(7)) comparator_3 (
    .a(inst[31:25]), .b({7{1'b0}}), .eq(comparator_3_eq));  // open: gt, lt
  Comparator #(.mode("unsigned"), .width(7)) comparator_4 (
    .a(inst[31:25]), .b({7{1'b0}}), .eq(comparator_4_eq));  // open: gt, lt
  Comparator #(.mode("unsigned"), .width(7)) comparator_5 (
    .a(inst[31:25]), .b({7{1'b0}}), .eq(comparator_5_eq));  // open: gt, lt
  or or_1 (or_1_out, not_1_out, BrEq);
  Multiplexer #(.enable("false"), .width(4)) multiplexer_1 (
    .in0(4'b1100), .in1(4'b1000), .out(multiplexer_1_out), .sel(comparator_1_eq));
  or or_2 (or_2_out, comparator_2_eq, comparator_3_eq);
  not not_2 (not_2_out, BrEq);
  Comparator #(.mode("unsigned"), .width(7)) comparator_6 (
    .a(inst[6:0]), .b(7'b1100011), .eq(comparator_6_eq));  // open: gt, lt
  Comparator #(.mode("unsigned"), .width(7)) comparator_7 (
    .a(inst[6:0]), .b(7'b0100011), .eq(comparator_7_eq));  // open: gt, lt
  Multiplexer #(.enable("false"), .select(3)) multiplexer_2 (
    .in0(1'b1), .in1(1'b1), .in4(1'b0), .in5(1'b0), .in6(1'b1), .in7(1'b1), .out(multiplexer_2_out),
    .sel(inst[14:12]));  // open: in2, in3
  Comparator #(.mode("unsigned"), .width(7)) comparator_8 (
    .a(inst[6:0]), .b(7'b1100011), .eq(comparator_8_eq));  // open: gt, lt
  ROM #(.addrWidth(6), .dataWidth(16)) rom_1 (.data(rom_1_data));  // open: addr
  Multiplexer #(.enable("false"), .width(4)) multiplexer_3 (
    .in0(multiplexer_1_out), .in1(4'b0000), .out(multiplexer_3_out), .sel(or_2_out));
  Multiplexer #(.enable("false"), .width(4)) multiplexer_4 (
    .in0(4'b1001), .in1(4'b0001), .out(multiplexer_4_out), .sel(comparator_4_eq));
  Multiplexer #(.enable("false"), .width(4)) multiplexer_5 (
    .in0(4'b1101), .in1(4'b0101), .out(multiplexer_5_out), .sel(comparator_5_eq));
  Multiplexer #(.enable("false"), .select(3)) multiplexer_6 (
    .in0(BrEq), .in1(not_2_out), .in4(BrLt), .in5(or_1_out), .in6(BrLt), .in7(or_1_out),
    .out(multiplexer_6_out), .sel(inst[14:12]));  // open: in2, in3
  Comparator #(.mode("unsigned"), .width(7)) comparator_9 (
    .a(inst[6:0]), .b(7'b1100011), .eq(comparator_9_eq));  // open: gt, lt
  Multiplexer #(.enable("false")) multiplexer_7 (
    .in0(1'b0), .in1(multiplexer_2_out), .out(BrUn), .sel(comparator_8_eq));
  Comparator #(.mode("unsigned"), .width(7)) comparator_10 (
    .a(inst[6:0]), .b(7'b1110011), .eq(CSRWen));  // open: gt, lt
  Multiplexer #(.enable("false")) multiplexer_8 (.in0(1'b1), .in1(1'b0), .out(RegWEn), .sel(or_3_out));
  or or_3 (or_3_out, comparator_9_eq, comparator_7_eq);
  Comparator #(.mode("unsigned"), .width(7)) comparator_11 (
    .a(inst[6:0]), .b(7'b1101111), .eq(comparator_11_eq));  // open: gt, lt
  Comparator #(.mode("unsigned"), .width(7)) comparator_12 (
    .a(inst[6:0]), .b(7'b1100111), .eq(comparator_12_eq));  // open: gt, lt
  or or_4 (or_4_out, comparator_11_eq, comparator_12_eq);
  Multiplexer #(.enable("false")) multiplexer_9 (
    .in0(or_4_out), .in1(multiplexer_6_out), .out(PCSel), .sel(comparator_6_eq));
  Multiplexer #(.enable("false"), .select(3), .width(4)) multiplexer_10 (
    .in0(multiplexer_3_out), .in1(multiplexer_4_out), .in2(4'b0010), .in3(4'b1011), .in4(4'b0100),
    .in5(multiplexer_5_out), .in6(4'b0110), .in7(4'b0111), .out(multiplexer_10_out), .sel(inst[14:12]));
  Comparator #(.mode("unsigned"), .width(7)) comparator_13 (
    .a(inst[6:0]), .b(7'b1100011), .eq(comparator_13_eq));  // open: gt, lt
  Comparator #(.mode("unsigned"), .width(7)) comparator_14 (
    .a(inst[6:0]), .b(7'b1101111), .eq(comparator_14_eq));  // open: gt, lt
  Comparator #(.mode("unsigned"), .width(7)) comparator_15 (
    .a(inst[6:0]), .b(7'b0010111), .eq(comparator_15_eq));  // open: gt, lt
  Comparator #(.mode("unsigned"), .width(7)) comparator_16 (.a(inst[6:0]), .b(7'b0100011), .eq(MemRW));  // open: gt, lt
  or or_5 (ASel, comparator_13_eq, comparator_14_eq, comparator_15_eq);
  Comparator #(.mode("unsigned"), .width(7)) comparator_17 (.a(inst[6:0]), .b(7'b0110011), .eq(BSel));  // open: gt, lt
  Comparator #(.mode("unsigned"), .width(7)) comparator_18 (
    .a(inst[6:0]), .b(7'b1100111), .eq(comparator_18_eq));  // open: gt, lt
  Comparator #(.mode("unsigned"), .width(7)) comparator_19 (
    .a(inst[6:0]), .b(7'b0010011), .eq(comparator_19_eq));  // open: gt, lt
  Comparator #(.mode("unsigned"), .width(7)) comparator_20 (
    .a(inst[6:0]), .b(7'b0110011), .eq(comparator_20_eq));  // open: gt, lt
  Comparator #(.mode("unsigned"), .width(7)) comparator_21 (
    .a(inst[6:0]), .b(7'b0010011), .eq(comparator_21_eq));  // open: gt, lt
  or or_6 (or_6_out, comparator_18_eq, comparator_19_eq);
  Comparator #(.mode("unsigned"), .width(7)) comparator_22 (
    .a(inst[6:0]), .b(7'b1100011), .eq(comparator_22_eq));  // open: gt, lt
  Comparator #(.mode("unsigned"), .width(7)) comparator_23 (
    .a(inst[6:0]), .b(7'b0100011), .eq(comparator_23_eq));  // open: gt, lt
  Comparator #(.mode("unsigned"), .width(7)) comparator_24 (
    .a(inst[6:0]), .b(7'b1101111), .eq(comparator_24_eq));  // open: gt, lt
  or or_7 (or_7_out, comparator_20_eq, comparator_21_eq);
  Comparator #(.mode("unsigned"), .width(7)) comparator_25 (
    .a(inst[6:0]), .b(7'b1101111), .eq(comparator_25_eq));  // open: gt, lt
  Comparator #(.mode("unsigned"), .width(7)) comparator_26 (
    .a(inst[6:0]), .b(7'b1100111), .eq(comparator_26_eq));  // open: gt, lt
  Comparator #(.mode("unsigned"), .width(7)) comparator_27 (
    .a(inst[6:0]), .b(7'b0110111), .eq(comparator_27_eq));  // open: gt, lt
  Multiplexer #(.enable("false"), .width(3)) multiplexer_11 (.in1(3'b000), .out(ImmSel), .sel(or_6_out));  // open: in0
  Multiplexer #(.enable("false"), .width(3)) multiplexer_12 (
    .in1(3'b010), .out(ImmSel), .sel(comparator_22_eq));  // open: in0
  Multiplexer #(.enable("false"), .width(3)) multiplexer_13 (
    .in1(3'b001), .out(ImmSel), .sel(comparator_23_eq));  // open: in0
  Multiplexer #(.enable("false"), .width(3)) multiplexer_14 (
    .in1(3'b100), .out(ImmSel), .sel(comparator_24_eq));  // open: in0
  or or_8 (or_8_out, comparator_25_eq, comparator_26_eq);
  Multiplexer #(.enable("false"), .width(4)) multiplexer_15 (
    .in0(4'b0000), .in1(4'b1111), .out(multiplexer_15_out), .sel(comparator_27_eq));
  Comparator #(.mode("unsigned"), .width(7)) comparator_28 (
    .a(inst[6:0]), .b(7'b0000011), .eq(comparator_28_eq));  // open: gt, lt
  Comparator #(.mode("unsigned"), .width(7)) comparator_29 (
    .a(inst[6:0]), .b(7'b1110011), .eq(comparator_29_eq));  // open: gt, lt
  Comparator #(.mode("unsigned"), .width(3)) comparator_30 (
    .a(inst[14:12]), .b(3'b101), .eq(comparator_30_eq));  // open: gt, lt
  Multiplexer #(.enable("false"), .width(2)) multiplexer_16 (
    .in0(2'b01), .in1(2'b10), .out(multiplexer_16_out), .sel(or_8_out));
  and and_1 (CSRSel, comparator_29_eq, comparator_30_eq);
  Multiplexer #(.enable("false"), .width(4)) multiplexer_17 (
    .in0(multiplexer_15_out), .in1(multiplexer_10_out), .out(ALUSel), .sel(or_7_out));
  Comparator #(.mode("unsigned"), .width(7)) comparator_31 (
    .a(inst[6:0]), .b(7'b0010111), .eq(comparator_31_eq));  // open: gt, lt
  Comparator #(.mode("unsigned"), .width(7)) comparator_32 (
    .a(inst[6:0]), .b(7'b0110111), .eq(comparator_32_eq));  // open: gt, lt
  Comparator #(.mode("unsigned"), .width(7)) comparator_33 (
    .a(inst[6:0]), .b(7'b1110011), .eq(comparator_33_eq));  // open: gt, lt
  Multiplexer #(.enable("false"), .width(2)) multiplexer_18 (
    .in0(multiplexer_16_out), .in1(2'b00), .out(WBSel), .sel(comparator_28_eq));
  or or_9 (or_9_out, comparator_31_eq, comparator_32_eq);
  Multiplexer #(.enable("false"), .width(3)) multiplexer_19 (
    .in1(3'b101), .out(ImmSel), .sel(comparator_33_eq));  // open: in0
  Multiplexer #(.enable("false"), .width(3)) multiplexer_20 (.in1(3'b011), .out(ImmSel), .sel(or_9_out));  // open: in0

  // Other names for the same wires on the sheet: OPCODE[6:0] = inst[6:0]; func3[2:0] = inst[14:12];
  //   func7[6:0] = inst[31:25]

  // Notes on the sheet:
  //   INPUTS to your circuit
  //   Connect ROM Input here ->
  //   ROM FOR CONTROL LOGIC
  //   DON'T CHANGE THE LOCATIONS OF THE INPUTS AND OUTPUTS!
  //   OUTPUT from your circuit
  //   CLOSE
  //   WIRE
  //   TO
  //   USE
  //   ROM
  //   Reminder: Use combinational logic for PCSel
endmodule
