// Logisim project cpu.circ as structural Verilog: 1 circuit, main circuit cpu
module cpu (
  input  clk,
  input  [31:0] INSTRUCTION,
  input  [31:0] MEM_READ_DATA,
  output [31:0] MEM_WRITE_ADDRESS,
  output [31:0] PROGRAM_COUNTER,
  output [31:0] ra,
  output [31:0] sp,
  output [31:0] t0,
  output [31:0] t1,
  output [31:0] t2,
  output [31:0] s0,
  output [31:0] s1,
  output [31:0] a0,
  output [31:0] tohost,
  output [3:0] MEM_WRITE_ENABLE,
  output [31:0] MEM_WRITE_DATA
);

  wire and_1_out, ASel, BrEq, BrLt, BrUn, BSel, comparator_1_eq, comparator_2_eq, comparator_3_eq,
       comparator_4_eq, comparator_5_eq, control_logic_1_csrsel, control_logic_1_csrwen, MemRW, or_1_out,
       or_2_out, PCSel, RegWEn;
  wire [1:0] WBSel;
  wire [2:0] func3, ImmSel;
  wire [3:0] ALUSel, multiplexer_9_out, multiplexer_10_out, multiplexer_12_out;
  wire [11:0] CSR_Address;
  wire [19:0] INSTRUCTION_t;
  wire [31:0] adder_1_out, bit_extender_1_out, bit_extender_2_out, bit_extender_3_out, bit_extender_4_out,
       immediate, multiplexer_1_out, multiplexer_2_out, multiplexer_3_out, multiplexer_4_out,
       multiplexer_5_out, multiplexer_7_out, multiplexer_8_out, multiplexer_11_out, PcPlusFour,
       PROGRAM_COUNTER_t, Read_Data, rs1_value, write_data;

  Adder #(.width(32)) adder_1 (.a(PROGRAM_COUNTER), .b(32'h4), .out(adder_1_out));  // open: cin, cout
  Multiplexer #(.enable("false"), .width(32)) multiplexer_1 (
    .in0(adder_1_out), .in1(MEM_WRITE_ADDRESS), .out(multiplexer_1_out), .sel(PCSel));
  Register #(.width(32)) PC (.D(multiplexer_1_out), .clk(clk), .Q(PROGRAM_COUNTER));  // open: en, clr
  Register #(.width(32)) register_1 (.D(PROGRAM_COUNTER), .clk(clk), .Q(PROGRAM_COUNTER_t));  // open: en, clr
  Comparator #(.mode("unsigned"), .width(7)) comparator_1 (
    .a(INSTRUCTION_t[6:0]), .b(7'b1101111), .eq(comparator_1_eq));  // open: gt, lt
  Comparator #(.mode("unsigned"), .width(7)) comparator_2 (
    .a(INSTRUCTION_t[6:0]), .b(7'b1100111), .eq(comparator_2_eq));  // open: gt, lt
  Comparator #(.mode("unsigned"), .width(7)) comparator_3 (
    .a(INSTRUCTION_t[6:0]), .b(7'b1100011), .eq(comparator_3_eq));  // open: gt, lt
  Comparator #(.mode("unsigned"), .width(1)) comparator_4 (.a(PCSel), .b(1'b1), .eq(comparator_4_eq));  // open: gt, lt
  Adder #(.width(32)) adder_2 (.a(PROGRAM_COUNTER_t), .b(32'h4), .out(PcPlusFour));  // open: cin, cout
  control_logic control_logic_1 (
    .CSRWen(control_logic_1_csrwen), .PCSel(PCSel), .RegWEn(RegWEn), .ImmSel(ImmSel), .BrUn(BrUn),
    .ASel(ASel), .BSel(BSel), .ALUSel(ALUSel), .MemRW(MemRW), .WBSel(WBSel), .CSRSel(control_logic_1_csrsel),
    .inst({CSR_Address, INSTRUCTION_t[19:15], func3, INSTRUCTION_t[11:0]}), .BrEq(BrEq), .BrLt(BrLt));
  or or_1 (or_1_out, comparator_1_eq, comparator_2_eq);
  and and_1 (and_1_out, comparator_3_eq, comparator_4_eq);
  Multiplexer #(.enable("false"), .width(32)) multiplexer_2 (
    .in0(INSTRUCTION), .in1({32{1'b0}}), .out(multiplexer_2_out), .sel(or_2_out));
  or or_2 (or_2_out, or_1_out, and_1_out);
  Register #(.width(32)) register_2 (
    .D(multiplexer_2_out), .clk(clk), .Q({CSR_Address, INSTRUCTION_t[19:15], func3, INSTRUCTION_t[11:0]}));  // open: en, clr
  imm_gen imm_gen_1 (
    .inst({CSR_Address, INSTRUCTION_t[19:15], func3, INSTRUCTION_t[11:0]}), .ImmSel(ImmSel), .imm(immediate));
  regfile regfile_1 (
    .rs1(INSTRUCTION_t[19:15]), .rs2(CSR_Address[4:0]), .rd(INSTRUCTION_t[11:7]), .Write_Data(write_data),
    .RegWEn(RegWEn), .clk(clk), .ra(ra), .sp(sp), .t0(t0), .t1(t1), .t2(t2), .s0(s0), .s1(s1), .a0(a0),
    .Read_Data_1(rs1_value), .Read_Data_2(MEM_WRITE_DATA));
  branch_comp branch_comp_1 (.rs1(rs1_value), .rs2(MEM_WRITE_DATA), .BrUn(BrUn), .BrEq(BrEq), .BrLt(BrLt));
  Multiplexer #(.enable("false"), .width(32)) multiplexer_3 (
    .in0(rs1_value), .in1(PROGRAM_COUNTER_t), .out(multiplexer_3_out), .sel(ASel));
  Multiplexer #(.enable("false"), .width(32)) multiplexer_4 (
    .in0(immediate), .in1(MEM_WRITE_DATA), .out(multiplexer_4_out), .sel(BSel));
  Multiplexer #(.enable("false"), .width(32)) multiplexer_5 (
    .in0(rs1_value), .in1(immediate), .out(multiplexer_5_out), .sel(control_logic_1_csrsel));
  alu alu_1 (.Result(MEM_WRITE_ADDRESS), .A(multiplexer_3_out), .B(multiplexer_4_out), .ALUSel(ALUSel));
  // csr csr_1: pin names not known; wires that end beside it: CSR_Address, multiplexer_5_out, control_logic_1_csrwen, clk, tohost
  Multiplexer #(.enable("false"), .select(2), .width(32)) multiplexer_6 (
    .in0(Read_Data), .in1(MEM_WRITE_ADDRESS), .in2(PcPlusFour), .out(write_data), .sel(WBSel));  // open: in3
  Comparator #(.mode("unsigned"), .width(7)) comparator_5 (
    .a(INSTRUCTION_t[6:0]), .b(7'b0000011), .eq(comparator_5_eq));  // open: gt, lt
  assign bit_extender_1_out = {{24{MEM_READ_DATA[7]}}, MEM_READ_DATA[7:0]};  // Bit_Extender bit_extender_1
  assign bit_extender_2_out = {{16{MEM_READ_DATA[15]}}, MEM_READ_DATA[15:0]};  // Bit_Extender bit_extender_2
  assign bit_extender_3_out = {{8{MEM_READ_DATA[23]}}, MEM_READ_DATA[23:0]};  // Bit_Extender bit_extender_3
  assign bit_extender_4_out = {{16{MEM_READ_DATA[15]}}, MEM_READ_DATA[15:0]};  // Bit_Extender bit_extender_4
  Multiplexer #(.enable("false"), .select(2), .width(32)) multiplexer_7 (
    .in0(bit_extender_1_out), .in1(bit_extender_2_out), .in2(bit_extender_3_out), .in3(MEM_READ_DATA),
    .out(multiplexer_7_out), .sel(MEM_WRITE_ADDRESS[1:0]));
  Multiplexer #(.enable("false"), .select(2), .width(32)) multiplexer_8 (
    .in0(bit_extender_4_out), .in2(MEM_READ_DATA), .out(multiplexer_8_out), .sel(MEM_WRITE_ADDRESS[1:0]));  // open: in1, in3
  Multiplexer #(.enable("false"), .select(2), .width(4)) multiplexer_9 (
    .in0(4'b0001), .in1(4'b0010), .in2(4'b0100), .in3(4'b1000), .out(multiplexer_9_out),
    .sel(MEM_WRITE_ADDRESS[1:0]));
  Multiplexer #(.enable("false"), .select(2), .width(4)) multiplexer_10 (
    .in0(4'b0011), .in2(4'b1100), .out(multiplexer_10_out), .sel(MEM_WRITE_ADDRESS[1:0]));  // open: in1, in3
  Multiplexer #(.enable("false"), .select(2), .width(32)) multiplexer_11 (
    .in0(multiplexer_7_out), .in1(multiplexer_8_out), .in2(MEM_READ_DATA), .out(multiplexer_11_out),
    .sel(func3[1:0]));  // open: in3
  Multiplexer #(.enable("false"), .select(2), .width(4)) multiplexer_12 (
    .in0(multiplexer_9_out), .in1(multiplexer_10_out), .in2(4'b1111), .out(multiplexer_12_out),
    .sel(func3[1:0]));  // open: in3
  Multiplexer #(.enable("false"), .width(32)) multiplexer_13 (
    .in1(multiplexer_11_out), .out(Read_Data), .sel(comparator_5_eq));  // open: in0
  Multiplexer #(.enable("false"), .width(4)) multiplexer_14 (
    .in0(4'b0000), .in1(multiplexer_12_out), .out(MEM_WRITE_ENABLE), .sel(MemRW));

  // Other names for the same wires on the sheet: ALU_Val[31:0] = MEM_WRITE_ADDRESS; OPCODE[6:0] = INSTRUCTION_t[6:0];
  //   rd[4:0] = INSTRUCTION_t[11:7]; INSTRUCTION_t (some bits) = {CSR_Address, func3};
  //   rs1[4:0] = INSTRUCTION_t[19:15]; rs2[4:0] = CSR_Address[4:0]; rs2_value[31:0] = MEM_WRITE_DATA

  // Notes on the sheet:
  //   Output to IMEM
  //   IMEM (do **NOT** move this)
  //   Inputs from IMEM
  //   Inputs/Outputs for testing. Do **NOT** move these.
  //   Outputs To DMEM
  //   DMEM (do **NOT** move this)
  //   Inputs From DMEM
endmodule
