// Logisim project imm-gen.circ as structural Verilog: 1 circuit, main circuit imm_gen
module imm_gen (
  input  [31:0] inst,
  input  [2:0] ImmSel,
  output [31:0] imm
);

  wire [12:0] bit_extender_4_out, shifter_2_out;
  wire [20:0] bit_extender_6_out, shifter_3_out;
  wire [31:0] bit_extender_2_out, CRS, I, S, SB, U, UJ;

  assign I = {{20{inst[31]}}, inst[31:20]};  // Bit_Extender bit_extender_1
  assign bit_extender_2_out = {{12{1'b0}}, inst[31:12]};  // Bit_Extender bit_extender_2
  assign S = {{20{inst[31]}}, {inst[31:25], inst[11:7]}};  // Bit_Extender bit_extender_3
  Shifter #(.width(32)) shifter_1 (.in(bit_extender_2_out), .\dist (5'b01100), .out(U));
  assign bit_extender_4_out = {{1{1'b0}}, {inst[31], inst[7], inst[30:25], inst[11:8]}};  // Bit_Extender bit_extender_4
  assign CRS = {{27{1'b0}}, inst[19:15]};  // Bit_Extender bit_extender_5
  assign bit_extender_6_out = {{1{1'b0}}, {inst[31], inst[19:12], inst[20], inst[30:21]}};  // Bit_Extender bit_extender_6
  Shifter #(.width(13)) shifter_2 (.in(bit_extender_4_out), .\dist (4'b0001), .out(shifter_2_out));
  Shifter #(.width(21)) shifter_3 (.in(bit_extender_6_out), .\dist (5'b00001), .out(shifter_3_out));
  assign SB = {{19{shifter_2_out[12]}}, shifter_2_out};  // Bit_Extender bit_extender_7
  assign UJ = {{11{shifter_3_out[20]}}, shifter_3_out};  // Bit_Extender bit_extender_8
  Multiplexer #(.enable("false"), .select(3), .width(32)) multiplexer_1 (
    .in0(I), .in1(S), .in2(SB), .in3(U), .in4(UJ), .in5(CRS), .out(imm), .sel(ImmSel));  // open: in6, in7

  // Notes on the sheet:
  //   INPUTS to your circuit
  //   DON'T CHANGE THE LOCATIONS OF THE INPUTS AND OUTPUTS!
  //   OUTPUT from your circuit
endmodule
