// Logisim project regfile.circ as structural Verilog: 1 circuit, main circuit regfile
module regfile (
  input  [4:0] rs1,
  input  [4:0] rs2,
  input  [4:0] rd,
  input  [31:0] Write_Data,
  input  RegWEn,
  input  clk,
  output [31:0] ra,
  output [31:0] sp,
  output [31:0] t0,
  output [31:0] t1,
  output [31:0] t2,
  output [31:0] s0,
  output [31:0] s1,
  output [31:0] a0,
  output [31:0] Read_Data_1,
  output [31:0] Read_Data_2
);

  wire and_1_out, and_2_out, and_3_out, and_4_out, and_5_out, and_6_out, and_7_out, and_8_out, and_9_out,
       and_10_out, and_11_out, and_12_out, and_13_out, and_14_out, and_15_out, and_16_out, and_17_out,
       and_18_out, and_19_out, and_20_out, and_21_out, and_22_out, and_23_out, and_24_out, and_25_out,
       and_26_out, and_27_out, and_28_out, and_29_out, and_30_out, and_31_out, comparator_1_eq,
       comparator_2_eq, comparator_3_eq, comparator_4_eq, comparator_5_eq, comparator_6_eq, comparator_7_eq,
       comparator_8_eq, comparator_9_eq, comparator_10_eq, comparator_11_eq, comparator_12_eq,
       comparator_13_eq, comparator_14_eq, comparator_15_eq, comparator_16_eq, comparator_17_eq,
       comparator_18_eq, comparator_19_eq, comparator_20_eq, comparator_21_eq, comparator_22_eq,
       comparator_23_eq, comparator_24_eq, comparator_25_eq, comparator_26_eq, comparator_27_eq,
       comparator_28_eq, comparator_29_eq, comparator_30_eq, comparator_31_eq;
  wire [31:0] a0_data, a1, a1_data, a2, a2_data, a3, a3_data, a4, a4_data, a5, a5_data, a6, a6_data, a7,
       a7_data, gp, gp_data, ra_data, s0_data, s1_data, s2, s2_data, s3, s3_data, s4, s4_data, s5, s5_data,
       s6, s6_data, s7, s7_data, s8, s8_data, s9, s9_data, s10, s10_data, s11, s11_data, sp_data, t0_data,
       t1_data, t2_data, t3, t3_data, t4, t4_data, t5, t5_data, t6, t6_data, tp, tp_data;

  Comparator #(.mode("unsigned"), .width(5)) comparator_1 (.a(rd), .b(5'b00010), .eq(comparator_1_eq));  // open: gt, lt
  Comparator #(.mode("unsigned"), .width(5)) comparator_2 (.a(rd), .b(5'b00011), .eq(comparator_2_eq));  // open: gt, lt
  Comparator #(.mode("unsigned"), .width(5)) comparator_3 (.a(rd), .b(5'b00100), .eq(comparator_3_eq));  // open: gt, lt
  Comparator #(.mode("unsigned"), .width(5)) comparator_4 (.a(rd), .b(5'b00101), .eq(comparator_4_eq));  // open: gt, lt
  Comparator #(.mode("unsigned"), .width(5)) comparator_5 (.a(rd), .b(5'b00110), .eq(comparator_5_eq));  // open: gt, lt
  Comparator #(.mode("unsigned"), .width(5)) comparator_6 (.a(rd), .b(5'b00111), .eq(comparator_6_eq));  // open: gt, lt
  Comparator #(.mode("unsigned"), .width(5)) comparator_7 (.a(rd), .b(5'b01000), .eq(comparator_7_eq));  // open: gt, lt
  Comparator #(.mode("unsigned"), .width(5)) comparator_8 (.a(rd), .b(5'b01001), .eq(comparator_8_eq));  // open: gt, lt
  Comparator #(.mode("unsigned"), .width(5)) comparator_9 (.a(rd), .b(5'b01010), .eq(comparator_9_eq));  // open: gt, lt
  Comparator #(.mode("unsigned"), .width(5)) comparator_10 (
    .a(rd), .b(5'b01011), .eq(comparator_10_eq));  // open: gt, lt
  Comparator #(.mode("unsigned"), .width(5)) comparator_11 (
    .a(rd), .b(5'b01100), .eq(comparator_11_eq));  // open: gt, lt
  Comparator #(.mode("unsigned"), .width(5)) comparator_12 (
    .a(rd), .b(5'b01101), .eq(comparator_12_eq));  // open: gt, lt
  Comparator #(.mode("unsigned"), .width(5)) comparator_13 (
    .a(rd), .b(5'b01110), .eq(comparator_13_eq));  // open: gt, lt
  Comparator #(.mode("unsigned"), .width(5)) comparator_14 (
    .a(rd), .b(5'b01111), .eq(comparator_14_eq));  // open: gt, lt
  Demultiplexer #(.enable("false"), .select(5), .width(32)) demultiplexer_1 (
    .out1(ra_data), .out2(sp_data), .out3(gp_data), .out4(tp_data), .out5(t0_data), .out6(t1_data),
    .out7(t2_data), .out8(s0_data), .out9(s1_data), .out10(a0_data), .out11(a1_data), .out12(a2_data),
    .out13(a3_data), .out14(a4_data), .out15(a5_data), .out16(a6_data), .out17(a7_data), .out18(s2_data),
    .out19(s3_data), .out20(s4_data), .out21(s5_data), .out22(s6_data), .out23(s7_data), .out24(s8_data),
    .out25(s9_data), .out26(s10_data), .out27(s11_data), .out28(t3_data), .out29(t4_data), .out30(t5_data),
    .out31(t6_data), .in(Write_Data), .sel(rd));  // open: out0
  and and_1 (and_1_out, comparator_1_eq, RegWEn);
  and and_2 (and_2_out, comparator_2_eq, RegWEn);
  and and_3 (and_3_out, comparator_3_eq, RegWEn);
  and and_4 (and_4_out, comparator_4_eq, RegWEn);
  and and_5 (and_5_out, comparator_5_eq, RegWEn);
  and and_6 (and_6_out, comparator_6_eq, RegWEn);
  and and_7 (and_7_out, comparator_7_eq, RegWEn);
  and and_8 (and_8_out, comparator_8_eq, RegWEn);
  and and_9 (and_9_out, comparator_9_eq, RegWEn);
  and and_10 (and_10_out, comparator_10_eq, RegWEn);
  and and_11 (and_11_out, comparator_11_eq, RegWEn);
  and and_12 (and_12_out, comparator_12_eq, RegWEn);
  and and_13 (and_13_out, comparator_13_eq, RegWEn);
  and and_14 (and_14_out, comparator_14_eq, RegWEn);
  Comparator #(.mode("unsigned"), .width(5)) comparator_15 (
    .a(rd), .b(5'b00001), .eq(comparator_15_eq));  // open: gt, lt
  and and_15 (and_15_out, comparator_15_eq, RegWEn);
  Register #(.width(32)) x2 (.D(sp_data), .en(and_1_out), .clk(clk), .Q(sp));  // open: clr
  Register #(.width(32)) x4 (.D(tp_data), .en(and_3_out), .clk(clk), .Q(tp));  // open: clr
  Register #(.width(32)) x5 (.D(t0_data), .en(and_4_out), .clk(clk), .Q(t0));  // open: clr
  Register #(.width(32)) x1 (.D(ra_data), .en(and_15_out), .clk(clk), .Q(ra));  // open: clr
  Register #(.width(32)) x3 (.D(gp_data), .en(and_2_out), .clk(clk), .Q(gp));  // open: clr
  Register #(.width(32)) x6 (.D(t1_data), .en(and_5_out), .clk(clk), .Q(t1));  // open: clr
  Register #(.width(32)) x7 (.D(t2_data), .en(and_6_out), .clk(clk), .Q(t2));  // open: clr
  Register #(.width(32)) x8 (.D(s0_data), .en(and_7_out), .clk(clk), .Q(s0));  // open: clr
  Register #(.width(32)) x9 (.D(s1_data), .en(and_8_out), .clk(clk), .Q(s1));  // open: clr
  Register #(.width(32)) x10 (.D(a0_data), .en(and_9_out), .clk(clk), .Q(a0));  // open: clr
  Register #(.width(32)) x11 (.D(a1_data), .en(and_10_out), .clk(clk), .Q(a1));  // open: clr
  Register #(.width(32)) x12 (.D(a2_data), .en(and_11_out), .clk(clk), .Q(a2));  // open: clr
  Register #(.width(32)) x13 (.D(a3_data), .en(and_12_out), .clk(clk), .Q(a3));  // open: clr
  Register #(.width(32)) x14 (.D(a4_data), .en(and_13_out), .clk(clk), .Q(a4));  // open: clr
  Register #(.width(32)) x15 (.D(a5_data), .en(and_14_out), .clk(clk), .Q(a5));  // open: clr
  Comparator #(.mode("unsigned"), .width(5)) comparator_16 (
    .a(rd), .b(5'b10000), .eq(comparator_16_eq));  // open: gt, lt
  Comparator #(.mode("unsigned"), .width(5)) comparator_17 (
    .a(rd), .b(5'b10001), .eq(comparator_17_eq));  // open: gt, lt
  Comparator #(.mode("unsigned"), .width(5)) comparator_18 (
    .a(rd), .b(5'b10010), .eq(comparator_18_eq));  // open: gt, lt
  Comparator #(.mode("unsigned"), .width(5)) comparator_19 (
    .a(rd), .b(5'b10011), .eq(comparator_19_eq));  // open: gt, lt
  Comparator #(.mode("unsigned"), .width(5)) comparator_20 (
    .a(rd), .b(5'b10100), .eq(comparator_20_eq));  // open: gt, lt
  Comparator #(.mode("unsigned"), .width(5)) comparator_21 (
    .a(rd), .b(5'b10101), .eq(comparator_21_eq));  // open: gt, lt
  Comparator #(.mode("unsigned"), .width(5)) comparator_22 (
    .a(rd), .b(5'b10110), .eq(comparator_22_eq));  // open: gt, lt
  Comparator #(.mode("unsigned"), .width(5)) comparator_23 (
    .a(rd), .b(5'b10111), .eq(comparator_23_eq));  // open: gt, lt
  Comparator #(.mode("unsigned"), .width(5)) comparator_24 (
    .a(rd), .b(5'b11000), .eq(comparator_24_eq));  // open: gt, lt
  Comparator #(.mode("unsigned"), .width(5)) comparator_25 (
    .a(rd), .b(5'b11001), .eq(comparator_25_eq));  // open: gt, lt
  Comparator #(.mode("unsigned"), .width(5)) comparator_26 (
    .a(rd), .b(5'b11010), .eq(comparator_26_eq));  // open: gt, lt
  Comparator #(.mode("unsigned"), .width(5)) comparator_27 (
    .a(rd), .b(5'b11100), .eq(comparator_27_eq));  // open: gt, lt
  Comparator #(.mode("unsigned"), .width(5)) comparator_28 (
    .a(rd), .b(5'b11100), .eq(comparator_28_eq));  // open: gt, lt
  Comparator #(.mode("unsigned"), .width(5)) comparator_29 (
    .a(rd), .b(5'b11101), .eq(comparator_29_eq));  // open: gt, lt
  Comparator #(.mode("unsigned"), .width(5)) comparator_30 (
    .a(rd), .b(5'b11110), .eq(comparator_30_eq));  // open: gt, lt
  Comparator #(.mode("unsigned"), .width(5)) comparator_31 (
    .a(rd), .b({5{1'b1}}), .eq(comparator_31_eq));  // open: gt, lt
  and and_16 (and_16_out, comparator_16_eq, RegWEn);
  and and_17 (and_17_out, comparator_17_eq, RegWEn);
  and and_18 (and_18_out, comparator_18_eq, RegWEn);
  and and_19 (and_19_out, comparator_19_eq, RegWEn);
  and and_20 (and_20_out, comparator_20_eq, RegWEn);
  and and_21 (and_21_out, comparator_21_eq, RegWEn);
  and and_22 (and_22_out, comparator_22_eq, RegWEn);
  and and_23 (and_23_out, comparator_23_eq, RegWEn);
  and and_24 (and_24_out, comparator_24_eq, RegWEn);
  and and_25 (and_25_out, comparator_25_eq, RegWEn);
  and and_26 (and_26_out, comparator_26_eq, RegWEn);
  and and_27 (and_27_out, comparator_27_eq, RegWEn);
  and and_28 (and_28_out, comparator_28_eq, RegWEn);
  and and_29 (and_29_out, comparator_29_eq, RegWEn);
  and and_30 (and_30_out, comparator_30_eq, RegWEn);
  and and_31 (and_31_out, comparator_31_eq, RegWEn);
  Register #(.width(32)) x16 (.D(a6_data), .en(and_16_out), .clk(clk), .Q(a6));  // open: clr
  Register #(.width(32)) x17 (.D(a7_data), .en(and_17_out), .clk(clk), .Q(a7));  // open: clr
  Register #(.width(32)) x18 (.D(s2_data), .en(and_18_out), .clk(clk), .Q(s2));  // open: clr
  Register #(.width(32)) x19 (.D(s3_data), .en(and_19_out), .clk(clk), .Q(s3));  // open: clr
  Register #(.width(32)) x20 (.D(s4_data), .en(and_20_out), .clk(clk), .Q(s4));  // open: clr
  Register #(.width(32)) x21 (.D(s5_data), .en(and_21_out), .clk(clk), .Q(s5));  // open: clr
  Register #(.width(32)) x22 (.D(s6_data), .en(and_22_out), .clk(clk), .Q(s6));  // open: clr
  Register #(.width(32)) x23 (.D(s7_data), .en(and_23_out), .clk(clk), .Q(s7));  // open: clr
  Register #(.width(32)) x24 (.D(s8_data), .en(and_24_out), .clk(clk), .Q(s8));  // open: clr
  Register #(.width(32)) x25 (.D(s9_data), .en(and_25_out), .clk(clk), .Q(s9));  // open: clr
  Register #(.width(32)) x26 (.D(s10_data), .en(and_26_out), .clk(clk), .Q(s10));  // open: clr
  Register #(.width(32)) x27 (.D(s11_data), .en(and_27_out), .clk(clk), .Q(s11));  // open: clr
  Register #(.width(32)) x28 (.D(t3_data), .en(and_28_out), .clk(clk), .Q(t3));  // open: clr
  Register #(.width(32)) x29 (.D(t4_data), .en(and_29_out), .clk(clk), .Q(t4));  // open: clr
  Register #(.width(32)) x30 (.D(t5_data), .en(and_30_out), .clk(clk), .Q(t5));  // open: clr
  Register #(.width(32)) x31 (.D(t6_data), .en(and_31_out), .clk(clk), .Q(t6));  // open: clr
  Multiplexer #(.enable("false"), .select(5), .width(32)) multiplexer_1 (
    .in0({32{1'b0}}), .in1(ra), .in2(sp), .in3(gp), .in4(tp), .in5(t0), .in6(t1), .in7(t2), .in8(s0),
    .in9(s1), .in10(a0), .in11(a1), .in12(a2), .in13(a3), .in14(a4), .in15(a5), .in16(a6), .in17(a7),
    .in18(s2), .in19(s3), .in20(s4), .in21(s5), .in22(s6), .in23(s7), .in24(s8), .in25(s9), .in26(s10),
    .in27(s11), .in28(t3), .in29(t4), .in30(t5), .in31(t6), .out(Read_Data_1), .sel(rs1));
  Multiplexer #(.enable("false"), .select(5), .width(32)) multiplexer_2 (
    .in0({32{1'b0}}), .in1(ra), .in2(sp), .in3(gp), .in4(tp), .in5(t0), .in6(t1), .in7(t2), .in8(s0),
    .in9(s1), .in10(a0), .in11(a1), .in12(a2), .in13(a3), .in14(a4), .in15(a5), .in16(a6), .in17(a7),
    .in18(s2), .in19(s3), .in20(s4), .in21(s5), .in22(s6), .in23(s7), .in24(s8), .in25(s9), .in26(s10),
    .in27(s11), .in28(t3), .in29(t4), .in30(t5), .in31(t6), .out(Read_Data_2), .sel(rs2));

  // Other names for the same wires on the sheet: read_data1[31:0] = Read_Data_1; read_data2[31:0] = Read_Data_2;
  //   read_reg1[4:0] = rs1; read_reg2[4:0] = rs2; write_en = RegWEn; write_reg[4:0] = rd

  // Notes on the sheet:
  //   INPUTS to your circuit
  //   DON'T CHANGE THE LOCATIONS OF THE INPUTS AND OUTPUTS!
  //   These are DEBUG/TEST outputs from your circuit.
  //   OUTPUTS from your circuit
endmodule
